# Fritzing sketch BATMONKEYYRYY (saved by Fritzing 0.9.3b)
perfboards: 1

parts:
  Carte = Arduino Mega ADK (Rev3)
  Bluetooth = Bluetooth HC-05 Macho
  Alimentation(en_vrai_c'est_pas_des_piles) = 4 x AAA Battery Mount [part_number="5V 55A"]
  Moteur_1 = Basic Servo
  Moteur_2 = Basic Servo
  Moteur_3 = Basic Servo
  Moteur_4 = Basic Servo
  Moteur_5 = Basic Servo
  Moteur_8 = Basic Servo
  Moteur_6 = Basic Servo
  Moteur_7 = Basic Servo

nets:
  N1: Carte.D19/RX1, Bluetooth.TXD
  N2: Carte.D18/TX1, Bluetooth.RXD
  GND: Carte.GND, Bluetooth.GND
  N3: Carte.D10_PWM, Moteur_1.pulse
  N4: Carte.D8_PWM, Moteur_2.pulse
  N5: Carte.D2_PWM, Moteur_8.pulse
  N6: Carte.D3_PWM, Moteur_7.pulse
  N7: Carte.D4_PWM, Moteur_6.pulse
  N8: Carte.D5_PWM, Moteur_5.pulse
  N9: Carte.D6_PWM, Moteur_4.pulse
  N10: Carte.D7_PWM, Moteur_3.pulse
  5V: Carte.5V, Bluetooth.VCC
  N11: Alimentation(en_vrai_c'est_pas_des_piles).-, Moteur_1.gnd
